// Logisim project Control_Unit.circ as structural Verilog: 1 circuit, main circuit Control_Unit
module Control_Unit (
  input  [15:0] IR,
  input  SC_INR,
  input  CLR,
  input  CP,
  output I,
  output [11:0] Add
);

  wire decoder3x8_1_p1, decoder4x16_1_p1, decoder4x16_1_p2, decoder4x16_1_p3, decoder4x16_1_p4,
       decoder4x16_1_p5;

  // Decoder4x16 decoder4x16_1: pin names not known; wires that end beside it: decoder4x16_1_p1, decoder4x16_1_p2, decoder4x16_1_p3, decoder4x16_1_p4, decoder4x16_1_p5
  Bit4_Counter bit4_counter_1 (
    .INR(SC_INR), .CP(CP), .CLR(CLR), .A0(decoder4x16_1_p2), .A1(decoder4x16_1_p3), .A2(decoder4x16_1_p4),
    .A3(decoder4x16_1_p5));
  // Decoder3x8 decoder3x8_1: pin names not known; wires that end beside it: decoder3x8_1_p1, IR[14], IR[13], IR[12]

  assign Add = IR[11:0];
  assign I = IR[15];

  // Notes on the sheet:
  //   Operation Decoder
  //   Sequence Decoder
endmodule
