// Logisim project BasicComputer.circ as structural Verilog: 1 circuit, main circuit CompleteComputer
module CompleteComputer (
);

  wire bit16_alsu_1_p5, control_unit_1_p3, control_unit_1_p5, control_unit_1_p7, control_unit_1_p9,
       control_unit_1_p10, control_unit_1_p11, control_unit_1_p12, control_unit_1_p13, control_unit_1_p14,
       control_unit_1_p15, control_unit_1_p16, control_unit_1_p17, control_unit_1_p18, control_unit_1_p19,
       control_unit_1_p20, control_unit_1_p21, control_unit_1_p22, control_unit_1_p23, control_unit_1_p24,
       control_unit_1_p25, control_unit_1_p26, control_unit_1_p27, control_unit_1_p28, control_unit_1_p29,
       control_unit_1_p30, control_unit_1_p31, control_unit_1_p32, control_unit_1_p33, CP_out, Reset_out;
  wire [3:0] bit16_alsu_1_p1, bit16_alsu_1_p1_2, bit16_alsu_1_p1_3, bit16_alsu_1_p1_4, bit16_alsu_1_p2,
       bit16_alsu_1_p2_2, bit16_alsu_1_p2_3, bit16_alsu_1_p2_4, control_unit_1_p1, control_unit_1_p2,
       control_unit_1_p2_2, control_unit_1_p2_3, control_unit_1_p2_4, controlled_buffer_1_out,
       controlled_buffer_1_out_2, controlled_buffer_1_out_3, controlled_buffer_3_out, SC_a0;
  wire [7:0] INPR_a, OUTR_a;
  wire [11:0] AR_a, PC_a;
  wire [15:0] ram_1_dout, TR_a;

  Clock CP (.out(CP_out));
  Button Reset (.out(Reset_out));
  Bit4_Counter SC (
    .INR(1'b1), .CP(CP_out), .CLR(control_unit_1_p5), .A0(SC_a0[0]), .A1(SC_a0[1]), .A2(SC_a0[2]),
    .A3(SC_a0[3]));
  Hex_Digit_Display hex_digit_display_1 (.value(control_unit_1_p1));  // open: dp
  // Control_Unit control_unit_1: pin names not known; wires that end beside it: control_unit_1_p1, {control_unit_1_p2_4, control_unit_1_p2_3, control_unit_1_p2_2, control_unit_1_p2}, control_unit_1_p3, 1'b0, control_unit_1_p5, SC_a0, control_unit_1_p7, Reset_out, control_unit_1_p9, control_unit_1_p10, control_unit_1_p11, control_unit_1_p12, control_unit_1_p13, control_unit_1_p14, control_unit_1_p15, control_unit_1_p16, control_unit_1_p17, control_unit_1_p18, control_unit_1_p19, control_unit_1_p20, control_unit_1_p21, control_unit_1_p22, control_unit_1_p23, control_unit_1_p24, control_unit_1_p25, control_unit_1_p26, control_unit_1_p27, control_unit_1_p28, control_unit_1_p29, control_unit_1_p30, control_unit_1_p31, control_unit_1_p32, control_unit_1_p33
  Hex_Digit_Display hex_digit_display_2 (.value(SC_a0));  // open: dp
  // Bit16_ALSU bit16_alsu_1: pin names not known; wires that end beside it: {bit16_alsu_1_p1_4, bit16_alsu_1_p1_3, bit16_alsu_1_p1_2, bit16_alsu_1_p1}, {bit16_alsu_1_p2_4, bit16_alsu_1_p2_3, bit16_alsu_1_p2_2, bit16_alsu_1_p2}, control_unit_1_p1, control_unit_1_p3, bit16_alsu_1_p5
  RAM #(.addrWidth(12), .asyncread("true"), .dataWidth(16)) ram_1 (
    .addr(AR_a), .we(control_unit_1_p20), .oe(control_unit_1_p19), .clk(CP_out),
    .din({controlled_buffer_3_out, controlled_buffer_1_out_3, controlled_buffer_1_out_2, controlled_buffer_1_out}),
    .dout(ram_1_dout));
  Bit12_Register AR (
    .I({controlled_buffer_1_out_3, controlled_buffer_1_out_2, controlled_buffer_1_out}),
    .Load(control_unit_1_p11), .INR(control_unit_1_p12), .CLR(control_unit_1_p13), .CP(CP_out), .A(AR_a));  // open: C
  Bit12_Register PC (
    .I({controlled_buffer_1_out_3, controlled_buffer_1_out_2, controlled_buffer_1_out}),
    .Load(control_unit_1_p21), .INR(control_unit_1_p22), .CLR(control_unit_1_p23), .CP(CP_out), .A(PC_a));  // open: C
  Bit16_Register DR (
    .I({controlled_buffer_3_out, controlled_buffer_1_out_3, controlled_buffer_1_out_2, controlled_buffer_1_out}),
    .Load(control_unit_1_p14), .INR(control_unit_1_p15), .CLR(control_unit_1_p16), .CP(CP_out),
    .A({bit16_alsu_1_p2_4, bit16_alsu_1_p2_3, bit16_alsu_1_p2_2, bit16_alsu_1_p2}));  // open: C
  // Bit16_Register AC: pin names not known; wires that end beside it: bit16_alsu_1_p5, control_unit_1_p7, control_unit_1_p9, control_unit_1_p10, CP_out, {bit16_alsu_1_p1_4, bit16_alsu_1_p1_3, bit16_alsu_1_p1_2, bit16_alsu_1_p1}
  Bit8_Register INPR (.CLR(Reset_out), .CP(CP_out), .A(INPR_a));  // open: I, Load, INR, C
  Bit16_Register IR (
    .I({controlled_buffer_3_out, controlled_buffer_1_out_3, controlled_buffer_1_out_2, controlled_buffer_1_out}),
    .Load(control_unit_1_p17), .INR(1'b0), .CLR(control_unit_1_p18), .CP(CP_out),
    .A({control_unit_1_p2_4, control_unit_1_p2_3, control_unit_1_p2_2, control_unit_1_p2}));  // open: C
  Bit16_Register TR (
    .I({controlled_buffer_3_out, controlled_buffer_1_out_3, controlled_buffer_1_out_2, controlled_buffer_1_out}),
    .Load(control_unit_1_p24), .INR(control_unit_1_p25), .CLR(control_unit_1_p26), .CP(CP_out), .A(TR_a));  // open: C
  Bit8_Register OUTR (.CLR(Reset_out), .CP(CP_out), .A(OUTR_a));  // open: I, Load, INR, C
  Hex_Digit_Display hex_digit_display_3 (.value(ram_1_dout[15:12]));  // open: dp
  Hex_Digit_Display hex_digit_display_4 (.value(ram_1_dout[11:8]));  // open: dp
  Hex_Digit_Display hex_digit_display_5 (.value(AR_a[11:8]));  // open: dp
  Hex_Digit_Display hex_digit_display_6 (.value(AR_a[7:4]));  // open: dp
  Hex_Digit_Display hex_digit_display_7 (.value(PC_a[11:8]));  // open: dp
  Hex_Digit_Display hex_digit_display_8 (.value(PC_a[7:4]));  // open: dp
  Hex_Digit_Display hex_digit_display_9 (.value(bit16_alsu_1_p2_4));  // open: dp
  Hex_Digit_Display hex_digit_display_10 (.value(bit16_alsu_1_p2_3));  // open: dp
  Hex_Digit_Display hex_digit_display_11 (.value(bit16_alsu_1_p1_4));  // open: dp
  Hex_Digit_Display hex_digit_display_12 (.value(bit16_alsu_1_p1_3));  // open: dp
  Hex_Digit_Display hex_digit_display_13 (.value(INPR_a[7:4]));  // open: dp
  Hex_Digit_Display hex_digit_display_14 (.value(INPR_a[3:0]));  // open: dp
  Hex_Digit_Display hex_digit_display_15 (.value(control_unit_1_p2_4));  // open: dp
  Hex_Digit_Display hex_digit_display_16 (.value(control_unit_1_p2_3));  // open: dp
  Hex_Digit_Display hex_digit_display_17 (.value(TR_a[15:12]));  // open: dp
  Hex_Digit_Display hex_digit_display_18 (.value(TR_a[11:8]));  // open: dp
  Hex_Digit_Display hex_digit_display_19 (.value(OUTR_a[7:4]));  // open: dp
  Hex_Digit_Display hex_digit_display_20 (.value(OUTR_a[3:0]));  // open: dp
  Hex_Digit_Display hex_digit_display_21 (.value(ram_1_dout[7:4]));  // open: dp
  Hex_Digit_Display hex_digit_display_22 (.value(ram_1_dout[3:0]));  // open: dp
  Hex_Digit_Display hex_digit_display_23 (.value(AR_a[3:0]));  // open: dp
  Hex_Digit_Display hex_digit_display_24 (.value(PC_a[3:0]));  // open: dp
  Hex_Digit_Display hex_digit_display_25 (.value(bit16_alsu_1_p2_2));  // open: dp
  Hex_Digit_Display hex_digit_display_26 (.value(bit16_alsu_1_p2));  // open: dp
  Hex_Digit_Display hex_digit_display_27 (.value(bit16_alsu_1_p1_2));  // open: dp
  Hex_Digit_Display hex_digit_display_28 (.value(bit16_alsu_1_p1));  // open: dp
  Hex_Digit_Display hex_digit_display_29 (.value(control_unit_1_p2_2));  // open: dp
  Hex_Digit_Display hex_digit_display_30 (.value(control_unit_1_p2));  // open: dp
  Hex_Digit_Display hex_digit_display_31 (.value(TR_a[7:4]));  // open: dp
  Hex_Digit_Display hex_digit_display_32 (.value(TR_a[3:0]));  // open: dp
  assign {controlled_buffer_1_out_3, controlled_buffer_1_out_2, controlled_buffer_1_out} = control_unit_1_p27 ? AR_a : 12'bz;  // Controlled_Buffer controlled_buffer_1
  assign {controlled_buffer_1_out_3, controlled_buffer_1_out_2, controlled_buffer_1_out} = control_unit_1_p28 ? PC_a : 12'bz;  // Controlled_Buffer controlled_buffer_2
  assign {controlled_buffer_3_out, controlled_buffer_1_out_3, controlled_buffer_1_out_2, controlled_buffer_1_out} = control_unit_1_p29 ? {bit16_alsu_1_p2_4, bit16_alsu_1_p2_3, bit16_alsu_1_p2_2, bit16_alsu_1_p2} : 16'bz;  // Controlled_Buffer controlled_buffer_3
  Hex_Digit_Display hex_digit_display_33 (.value(controlled_buffer_3_out));  // open: dp
  assign {controlled_buffer_3_out, controlled_buffer_1_out_3, controlled_buffer_1_out_2, controlled_buffer_1_out} = control_unit_1_p30 ? {bit16_alsu_1_p1_4, bit16_alsu_1_p1_3, bit16_alsu_1_p1_2, bit16_alsu_1_p1} : 16'bz;  // Controlled_Buffer controlled_buffer_4
  Hex_Digit_Display hex_digit_display_34 (.value(controlled_buffer_1_out_3));  // open: dp
  Hex_Digit_Display hex_digit_display_35 (.value(controlled_buffer_1_out_2));  // open: dp
  assign {controlled_buffer_3_out, controlled_buffer_1_out_3, controlled_buffer_1_out_2, controlled_buffer_1_out} = control_unit_1_p31 ? {control_unit_1_p2_4, control_unit_1_p2_3, control_unit_1_p2_2, control_unit_1_p2} : 16'bz;  // Controlled_Buffer controlled_buffer_5
  assign {controlled_buffer_3_out, controlled_buffer_1_out_3, controlled_buffer_1_out_2, controlled_buffer_1_out} = control_unit_1_p33 ? ram_1_dout : 16'bz;  // Controlled_Buffer controlled_buffer_6
  Hex_Digit_Display hex_digit_display_36 (.value(controlled_buffer_1_out));  // open: dp
  assign {controlled_buffer_3_out, controlled_buffer_1_out_3, controlled_buffer_1_out_2, controlled_buffer_1_out} = control_unit_1_p32 ? TR_a : 16'bz;  // Controlled_Buffer controlled_buffer_7
endmodule
